// Logisim project ex4.circ as structural Verilog: 5 circuits, main circuit RotRight
module RotRight (
  input  [15:0] INPUT0,
  input  [3:0] AMOUNT,
  output [15:0] OUTPUT0
);

  wire [15:0] mux0_output, mux1_output, mux2_output, rot1_output, rot2_output, rot4_output, rot8_output;

  Multiplexer #(.width(16)) multiplexer_1 (.in0(INPUT0), .in1(rot1_output), .out(mux0_output), .sel(AMOUNT[0]));
  Multiplexer #(.width(16)) multiplexer_2 (.in0(mux0_output), .in1(rot2_output), .out(mux1_output), .sel(AMOUNT[1]));
  Multiplexer #(.width(16)) multiplexer_3 (.in0(mux1_output), .in1(rot4_output), .out(mux2_output), .sel(AMOUNT[2]));
  Multiplexer #(.width(16)) multiplexer_4 (.in0(mux2_output), .in1(rot8_output), .out(OUTPUT0), .sel(AMOUNT[3]));
  rot1 rot1_1 (.in_1(INPUT0), .out_2(rot1_output));
  rot2 rot2_1 (.in_1(mux0_output), .out_2(rot2_output));
  rot4 rot4_1 (.in_1(mux1_output), .out_2(rot4_output));
  rot8 rot8_1 (.in_1(mux2_output), .out_2(rot8_output));

  // Other names for the same wires on the sheet: amt_0 = AMOUNT[0]; amt_1 = AMOUNT[1]; amt_2 = AMOUNT[2];
  //   amt_3 = AMOUNT[3]; final_output[15:0] = OUTPUT0
endmodule

module rot1 (
  input  [15:0] in_1,
  output [15:0] out_2
);


  assign out_2 = {in_1[0], in_1[15:1]};

  // Other names for the same wires on the sheet: bit0 = in_1[0]
endmodule

module rot2 (
  input  [15:0] in_1,
  output [15:0] out_2
);


  assign out_2 = {in_1[1:0], in_1[15:2]};

  // Other names for the same wires on the sheet: bit0 = in_1[0]; bit1 = in_1[1]
endmodule

module rot4 (
  input  [15:0] in_1,
  output [15:0] out_2
);


  assign out_2 = {in_1[3:0], in_1[15:4]};

  // Other names for the same wires on the sheet: bit0 = in_1[0]; bit1 = in_1[1]; bit2 = in_1[2]; bit3 = in_1[3]
endmodule

module rot8 (
  input  [15:0] in_1,
  output [15:0] out_2
);

  wire [15:0] rot4_1_out_2;

  rot4 rot4_1 (.in_1(in_1), .out_2(rot4_1_out_2));
  rot4 rot4_2 (.in_1(rot4_1_out_2), .out_2(out_2));
endmodule
